// Digital circuit Casa_Automatica.dig as structural Verilog
module Casa_Automatica (
  input  Modo_Seguro,
  input  Janela_1,
  input  Janela_2,
  input  Janela_3,
  input  Porta,
  input  Porta_Trancada,
  input  Sensor_Crepuscular,
  input  Sensor_de_chuva,
  input  \Temperatura_média_abaixo_de_15 ,
  input  Caixa_A_com_menos_de_20,
  input  Caixa_A_com_menos_de_15,
  input  Caixa_B_cheia
);

  wire not_1_out, u_alerta_alt, u_Caixas_de_Agua_cab, u_Caixas_de_Agua_eva;

  not not_1 (not_1_out, Porta_Trancada);
  alerta #(.applicationType("GHDL"), .CodeFile("/home/aluno/Documentos/VHDL/Casa_Automática/CasaAutomatica_Alerta.vhdl")) u_alerta (
    .MS(Modo_Seguro), .J1(Janela_1), .J2(Janela_2), .J3(Janela_3), .P(Porta), .PT(not_1_out),
    .SC(Sensor_Crepuscular), .SCh(Sensor_de_chuva), .T(\Temperatura_média_abaixo_de_15 ), .ALT(u_alerta_alt));
  Caixas_de_Agua #(.applicationType("GHDL"), .CodeFile("/home/aluno/Documentos/VHDL/Casa_Automática/CasaAutomatica_Caixas.vhdl")) u_Caixas_de_Agua (
    .SA20(Caixa_A_com_menos_de_20), .SA15(Caixa_A_com_menos_de_15), .SB(Caixa_B_cheia),
    .CAB(u_Caixas_de_Agua_cab), .EVA(u_Caixas_de_Agua_eva));
  LED Sinal_de_alerta (.in(u_alerta_alt));
  LED \Caixa_A_está_bombeando_para_B  (.in(u_Caixas_de_Agua_cab));
  LED \Eletroválvula_de_A_está_ligada  (.in(u_Caixas_de_Agua_eva));

  // Notes on the sheet:
  //   Explicação dos casos de teste:
  //   1º ao 3º = Alerta ativado se alguma janela estiver aberta com o modo seguro ativado;
  //   4º = Alerta ativado se porta estiver aberta mas trancada;
  //   5º = Alerta desativado se o modo seguro estiver ligado, a porta aberta mas destrancada;
  //   6º = Alerta desativado se todas janelas e a porta estiverem aberta mas o modo seguro desativado;
  //   7º = Alerta ativado se a porta estiver aberta mas trancada;
  //   8º ao 10º = Alerta ativado se estiver chovendo e alguma porta ou janela estiver aberta;
  //   11º = Alarme desativado se for a noite e a porta estiver aberta mas destrancada;
  //   12º ao 14º = Alarme ativado se for a noite e alguma das janelas estiver aberta;
  //   15º ao 17º = Alarme ativado se a temperatura estiver baixa e alguma janela estiver aberta;
  //   18º = Alarme desativado se a temperatura estiver baixa mas apenas a porta estiver aberta;
endmodule

/* Test case:
Modo_Seguro Janela_1 Janela_2 Janela_3 Porta Porta_Trancada Sensor_Crepuscular Sensor_de_chuva Temperatura_média_abaixo_de_15 Sinal_de_alerta
1 1 0 0 0 0 0 0 0 1
1 0 1 0 0 0 0 0 0 1
1 0 0 1 0 0 0 0 0 1
1 0 0 0 1 1 0 0 0 1
1 0 0 0 1 0 0 0 0 0
0 1 1 1 1 0 0 0 0 0
0 0 0 0 1 1 0 0 0 1
0 0 0 0 1 0 0 1 0 1
0 0 0 1 0 0 0 1 0 1
0 1 0 0 0 0 0 1 0 1
0 0 0 0 1 0 1 0 0 0
0 0 0 1 0 0 1 0 0 1
0 0 1 0 0 0 1 0 0 1
0 1 0 0 0 0 1 0 0 1
0 0 0 1 0 0 0 0 1 1
0 0 1 0 0 0 0 0 1 1
0 1 0 0 0 0 0 0 1 1
0 0 0 0 1 0 0 0 1 0
*/
