// Digital circuit Casa_Automatica.dig as structural Verilog
module Casa_Automatica (
  input  Caixa_B_cheia,
  input  [1:0] Sensor_de_A,
  input  Janela,
  input  Porta,
  input  Modo_Seguro
);

  wire [9:0] u_Casa_ledr;

  Casa #(.applicationType("GHDL"), .CodeFile("C:\\Users\\Pichau\\Documents\\C0de\\UFFS\\Sistemas\\Sistemas_2\\Casa_Automática(T1)\\Casa_automatica_main.vhd")) u_Casa (
    .sw({4'b0000, Caixa_B_cheia, Sensor_de_A, Porta, Janela, Modo_Seguro}), .ledr(u_Casa_ledr));
  LED Algo_estava_aberto_qaundo_MS_foi_ativado (.in(u_Casa_ledr[0]));
  LED Alguma_coisa_foi_aberta_durante_MS (.in(u_Casa_ledr[1]));
  LED \Entrada_Inválida__10  (.in(u_Casa_ledr[7]));
  LED \Caixa_A_está_bombeando_para_B  (.in(u_Casa_ledr[9]));
  LED \Eletroválvula_de_A_está_ligada  (.in(u_Casa_ledr[8]));
endmodule
