// Digital circuit ex5.dig as structural Verilog
module ex5 (
);

  demux #(.applicationType("GHDL"), .CodeFile("C:\\Users\\Softex\\Documents\\UFFS\\Sistemas\\Sistemas_2\\Exercicios\\ex5.vhd")) u_demux ();  // open: I0, I1, I2, I3, I4, I5, I6, I7, SEL, NUM
endmodule
