// Digital circuit pontuacao.dig as structural Verilog
module pontuacao (
  input  in_1,
  input  [3:0] in_2,
  input  in_3,
  input  in_4,
  output [4:0] out_5,
  output [1:0] out_6
);

  wire button_1_out, button_2_out, u_dealer_getcard, u_dealer_over, u_player_getcard, u_player_over,
       u_pontuacao_startdealer;
  wire [4:0] u_dealer_currentv, u_player_currentv;

  Button button_1 (.out(button_1_out));
  Button button_2 (.out(button_2_out));
  dealer #(.applicationType("GHDL"), .CodeFile("C:\\Users\\Softex\\Documents\\UFFS\\Sistemas\\Sistemas_2\\TF\\dealer.vhd")) u_dealer (
    .start(u_pontuacao_startdealer), .clock(button_2_out), .reset(button_1_out), .nextCard(in_2),
    .getCard(u_dealer_getcard), .currentV(u_dealer_currentv), .over(u_dealer_over));
  player #(.applicationType("GHDL"), .CodeFile("C:\\Users\\Softex\\Documents\\UFFS\\Sistemas\\Sistemas_2\\TF\\player.vhd")) u_player (
    .Hit(in_3), .start(in_1), .clock(button_2_out), .reset(button_1_out), .stay(in_4), .nextCard(in_2),
    .getCard(u_player_getcard), .currentV(u_player_currentv), .over(u_player_over));
  LED led_1 (.in(u_dealer_getcard));
  LED led_2 (.in(u_player_getcard));
  pontuacao #(.applicationType("GHDL"), .CodeFile("C:\\Users\\Softex\\Documents\\UFFS\\Sistemas\\Sistemas_2\\TF\\pontuacao.vhd")) u_pontuacao (
    .Stay_Player(u_player_over), .points_player(u_player_currentv), .stay_dealer(u_dealer_over),
    .points_dealer(u_dealer_currentv), .reset(button_1_out), .clock(button_2_out),
    .startDealer(u_pontuacao_startdealer), .result(out_6), .pointsShown(out_5));
endmodule
